// Logisim project week2.circ as structural Verilog: 4 circuits, main circuit main
module main (
  input  in_1,
  input  in_2,
  input  in_3
);

  wire and_1_out, or_1_out;

  and and_1 (and_1_out, in_1, in_2, in_3);
  or or_1 (or_1_out, in_1, in_2, in_3);
  LED led_1 (.in(and_1_out));
  LED led_2 (.in(or_1_out));
endmodule

module xorGate (
  input  in_1,
  input  in_2
);

  wire and_1_out, and_2_out, and_3_out, and_4_out, not_1_out, not_2_out, not_3_out, not_4_out, or_1_out,
       or_2_out, xnor_1_out, xor_1_out;

  not not_1 (not_1_out, in_1);
  not not_2 (not_2_out, in_2);
  not not_3 (not_3_out, in_1);
  not not_4 (not_4_out, in_2);
  xor xor_1 (xor_1_out, in_1, in_2);
  xnor xnor_1 (xnor_1_out, in_1, in_2);
  and and_1 (and_1_out, not_1_out, not_2_out);
  LED led_1 (.in(xor_1_out));
  LED led_2 (.in(xnor_1_out));
  and and_2 (and_2_out, not_3_out, in_2);
  and and_3 (and_3_out, in_1, not_4_out);
  and and_4 (and_4_out, in_1, in_2);
  or or_1 (or_1_out, and_2_out, and_3_out);
  or or_2 (or_2_out, and_4_out, and_1_out);
  LED led_3 (.in(or_1_out));
  LED led_4 (.in(or_2_out));

  // Notes on the sheet:
  //   a'b+ab'
  //   a'b'+ab
  //   XOR
  //   XNOR
endmodule

module splitterCircuit (
  input  [1:0] in_1,
  input  [1:0] in_2,
  input  [2:0] in_3,
  output [1:0] out_4
);

  wire and_2_out;

  assign out_4 = in_1 & in_2;  // AND_Gate and_1, 2 bits wide
  and and_2 (and_2_out, in_3[0], in_3[1], in_3[2]);
  LED led_1 (.in(and_2_out));
endmodule

module functionCircuit (
  input  [2:0] ABC
);

  wire and_1_out, and_2_out, and_3_out, and_4_out, not_1_out, not_2_out, not_3_out, or_1_out;

  not not_1 (not_1_out, ABC[2]);
  not not_2 (not_2_out, ABC[1]);
  not not_3 (not_3_out, ABC[0]);
  and and_1 (and_1_out, ABC[2], not_2_out, ABC[0]);
  and and_2 (and_2_out, not_1_out, ABC[1], not_3_out);
  and and_3 (and_3_out, not_1_out, not_2_out, ABC[0]);
  and and_4 (and_4_out, not_1_out, not_2_out, not_3_out);
  or or_1 (or_1_out, and_1_out, and_2_out, and_3_out, and_4_out);
  LED led_1 (.in(or_1_out));
endmodule
