// Logisim project week4.2.circ as structural Verilog: 3 circuits, main circuit main
module main (
  input  [3:0] A,
  input  [3:0] B,
  input  Bin,
  input  [3:0] in_4,
  input  [3:0] in_5,
  input  A_2,
  input  B_2,
  input  Bin_2,
  output [3:0] out_9,
  output out_10,
  output [3:0] out_11,
  output D,
  output Bout,
  output Bout_2
);

  wire and_1_out, and_2_out, and_3_out, and_4_out, and_5_out, and_6_out, and_7_out, and_8_out, and_9_out,
       and_10_out, not_1_out, not_2_out, not_3_out, not_4_out, not_5_out, not_6_out, not_7_out, not_8_out,
       not_9_out, not_10_out, or_2_out, or_3_out, or_4_out, xor_1_out, xor_3_out, xor_4_out, xor_5_out,
       xor_6_out;

  not not_1 (not_1_out, A_2);
  Subtractor #(.width(4)) subtractor_1 (.a(in_4), .b(in_5), .out(out_9), .bin(1'b0), .bout(out_10));
  xor xor_1 (xor_1_out, A_2, B_2);
  and and_1 (and_1_out, not_1_out, B_2);
  not not_2 (not_2_out, xor_1_out);
  xor xor_2 (D, xor_1_out, Bin_2);
  and and_2 (and_2_out, not_2_out, Bin_2);
  or or_1 (Bout, and_1_out, and_2_out);
  not not_3 (not_3_out, A[0]);
  not not_4 (not_4_out, A[1]);
  not not_5 (not_5_out, A[2]);
  not not_6 (not_6_out, A[3]);
  xor xor_3 (xor_3_out, A[0], B[0]);
  and and_3 (and_3_out, not_3_out, B[0]);
  xor xor_4 (xor_4_out, A[1], B[1]);
  and and_4 (and_4_out, not_4_out, B[1]);
  xor xor_5 (xor_5_out, A[2], B[2]);
  and and_5 (and_5_out, not_5_out, B[2]);
  xor xor_6 (xor_6_out, A[3], B[3]);
  and and_6 (and_6_out, not_6_out, B[3]);
  not not_7 (not_7_out, xor_3_out);
  not not_8 (not_8_out, xor_4_out);
  not not_9 (not_9_out, xor_5_out);
  not not_10 (not_10_out, xor_6_out);
  xor xor_7 (out_11[0], xor_3_out, Bin);
  and and_7 (and_7_out, not_7_out, Bin);
  xor xor_8 (out_11[1], xor_4_out, or_2_out);
  and and_8 (and_8_out, not_8_out, or_2_out);
  xor xor_9 (out_11[2], xor_5_out, or_3_out);
  and and_9 (and_9_out, not_9_out, or_3_out);
  xor xor_10 (out_11[3], xor_6_out, or_4_out);
  and and_10 (and_10_out, not_10_out, or_4_out);
  or or_2 (or_2_out, and_3_out, and_7_out);
  or or_3 (or_3_out, and_4_out, and_8_out);
  or or_4 (or_4_out, and_5_out, and_9_out);
  or or_5 (Bout_2, and_6_out, and_10_out);

  // Notes on the sheet:
  //   4 bit full subtactor
  //   1 bit full subtractor
  //   A0
  //   B0
  //   A1
  //   B1
  //   Bin
  //   A2
  //   B2
  //   Bin
  //   A3
  //   B3
  //   Bin
  //   4 bit full subtractor
  //   D
  //   D
  //   D
  //   D
  //   Bout
  //   Bout
  //   Bout
endmodule

module subtractors (
  input  [4:0] A,
  input  [4:0] B,
  input  [3:0] A_2,
  input  [3:0] B_2,
  input  [4:0] A_3,
  input  [4:0] B_3,
  output [3:0] out_7,
  output [5:0] out_8,
  output out_9,
  output out_10,
  output [4:0] out_11,
  output out_12
);

  wire adder_1_cout, adder_2_cout, adder_3_cout, adder_4_cout, adder_6_cout, adder_7_cout, adder_8_cout,
       adder_9_cout, not_1_out, not_2_out, not_3_out, not_4_out, not_5_out, subtractor_1_bout,
       subtractor_2_bout, subtractor_3_bout;

  not not_1 (not_1_out, B_3[4]);
  not not_2 (not_2_out, B_3[3]);
  not not_3 (not_3_out, B_3[2]);
  not not_4 (not_4_out, B_3[1]);
  not not_5 (not_5_out, B_3[0]);
  Subtractor #(.width(1)) subtractor_1 (.a(A_2[0]), .b(B_2[0]), .out(out_7[0]), .bin(1'b0), .bout(subtractor_1_bout));
  Subtractor #(.width(1)) subtractor_2 (
    .a(A_2[1]), .b(B_2[1]), .out(out_7[1]), .bin(subtractor_1_bout), .bout(subtractor_2_bout));
  Subtractor #(.width(1)) subtractor_3 (
    .a(A_2[2]), .b(B_2[2]), .out(out_7[2]), .bin(subtractor_2_bout), .bout(subtractor_3_bout));
  Subtractor #(.width(1)) subtractor_4 (.a(A_2[3]), .b(B_2[3]), .out(out_7[3]), .bin(subtractor_3_bout), .bout(out_9));
  Adder #(.width(1)) adder_1 (.a(A_3[0]), .b(not_5_out), .out(out_11[0]), .cin(1'b1), .cout(adder_1_cout));
  Adder #(.width(1)) adder_2 (.a(A_3[1]), .b(not_4_out), .out(out_11[1]), .cin(adder_1_cout), .cout(adder_2_cout));
  Adder #(.width(1)) adder_3 (.a(A_3[2]), .b(not_3_out), .out(out_11[2]), .cin(adder_2_cout), .cout(adder_3_cout));
  Adder #(.width(1)) adder_4 (.a(A_3[3]), .b(not_2_out), .out(out_11[3]), .cin(adder_3_cout), .cout(adder_4_cout));
  Adder #(.width(1)) adder_5 (.a(A_3[4]), .b(not_1_out), .out(out_11[4]), .cin(adder_4_cout), .cout(out_12));
  Adder #(.width(1)) adder_6 (.a(A[0]), .b(B[0]), .out(out_8[0]), .cin(1'b0), .cout(adder_6_cout));
  Adder #(.width(1)) adder_7 (.a(A[1]), .b(B[1]), .out(out_8[1]), .cin(adder_6_cout), .cout(adder_7_cout));
  Adder #(.width(1)) adder_8 (.a(A[2]), .b(B[2]), .out(out_8[2]), .cin(adder_7_cout), .cout(adder_8_cout));
  Adder #(.width(1)) adder_9 (.a(A[3]), .b(B[3]), .out(out_8[3]), .cin(adder_8_cout), .cout(adder_9_cout));
  Adder #(.width(1)) adder_10 (.a(A[4]), .b(B[4]), .out(out_8[4]), .cin(adder_9_cout), .cout(out_8[5]));

  assign out_10 = out_8[5];

  // Notes on the sheet:
  //   4 bit full subtractor
  //   5 bit subtractor using 5 bit adder
  //   0 => there is borrow
  //   1 => there isnt borrow
  //   5 bit full adder
endmodule

module sevenSegment (
  input  [3:0] ABCD
);

  wire and_1_out, and_2_out, and_3_out, and_4_out, and_5_out, and_6_out, and_7_out, and_8_out, and_9_out,
       and_10_out, and_11_out, and_12_out, and_13_out, and_14_out, and_15_out, and_16_out, not_1_out,
       not_2_out, not_3_out, not_4_out, or_1_out, or_2_out, or_3_out, or_4_out, or_5_out, or_6_out, or_7_out;

  not not_1 (not_1_out, ABCD[3]);
  not not_2 (not_2_out, ABCD[2]);
  not not_3 (not_3_out, ABCD[1]);
  not not_4 (not_4_out, ABCD[0]);
  and and_1 (and_1_out, not_2_out, not_4_out);
  and and_2 (and_2_out, ABCD[2], ABCD[0]);
  and and_3 (and_3_out, not_2_out, not_4_out);
  and and_4 (and_4_out, not_2_out, ABCD[1]);
  and and_5 (and_5_out, ABCD[2], not_3_out, ABCD[0]);
  and and_6 (and_6_out, ABCD[1], not_4_out);
  and and_7 (and_7_out, not_4_out, ABCD[1]);
  and and_8 (and_8_out, not_4_out, not_2_out);
  and and_9 (and_9_out, not_3_out, not_4_out);
  and and_10 (and_10_out, ABCD[2], not_3_out);
  and and_11 (and_11_out, ABCD[2], not_4_out);
  and and_12 (and_12_out, not_2_out, ABCD[1]);
  and and_13 (and_13_out, ABCD[2], not_3_out);
  and and_14 (and_14_out, ABCD[2], not_4_out);
  or or_1 (or_1_out, and_1_out, ABCD[1], and_2_out, ABCD[3]);
  and and_15 (and_15_out, not_3_out, not_4_out);
  and and_16 (and_16_out, ABCD[1], ABCD[0]);
  or or_2 (or_2_out, not_3_out, ABCD[2], ABCD[0]);
  or or_3 (or_3_out, and_7_out, and_8_out);
  or or_4 (or_4_out, and_12_out, and_13_out, ABCD[3], and_14_out);
  or or_5 (or_5_out, not_2_out, and_15_out, and_16_out);
  or or_6 (or_6_out, and_3_out, and_4_out, and_5_out, and_6_out, ABCD[3]);
  or or_7 (or_7_out, and_9_out, and_10_out, and_11_out, ABCD[3]);
  _7_Segment_Display #(.decimalPoint("false")) u_7_segment_display_1 (
    .g(or_4_out), .f(or_7_out), .a(or_1_out), .b(or_5_out), .e(or_3_out), .d(or_6_out), .c(or_2_out));

  // Notes on the sheet:
  //   a
  //   b
  //   c
  //   d
  //   e
  //   f
  //   g
endmodule
