// Logisim project week4.circ as structural Verilog: 2 circuits, main circuit main
module main (
  input  A,
  input  B,
  input  A_2,
  input  B_2,
  input  [1:0] A_3,
  input  Cin,
  input  [1:0] B_3,
  input  A_4,
  input  B_4,
  output S,
  output S_2,
  output Cout,
  output Cout_2,
  output [1:0] S_3,
  output S_4,
  output Cout_3,
  output Cout_4
);

  wire and_2_out, and_3_out, xor_2_out;

  // Probe on A_3
  // Probe on B_3
  xor xor_1 (S, A, B);
  and and_1 (Cout, B, A);
  Adder #(.width(2)) adder_1 (.a(A_3), .b(B_3), .out(S_3), .cout(Cout_4));  // open: cin
  // Probe on {Cout_4, S_3}
  Adder #(.width(1)) adder_2 (.a(A_2), .b(B_2), .out(S_2), .cout(Cout_2));  // open: cin
  xor xor_2 (xor_2_out, A_4, B_4);
  and and_2 (and_2_out, A_4, B_4);
  and and_3 (and_3_out, Cin, xor_2_out);
  xor xor_3 (S_4, Cin, xor_2_out);
  or or_1 (Cout_3, and_3_out, and_2_out);

  // Notes on the sheet:
  //   1 bit half adder
  //   2 bit half adder
  //   ANS
  //   1 bit half adder
  //   1 bit full adder
endmodule

module fullAdders (
  input  Cin,
  input  [1:0] A,
  input  Cin_2,
  input  [2:0] in_4,
  input  [1:0] B,
  input  [2:0] in_6,
  output [1:0] out_7,
  output [2:0] out_8,
  output Cout,
  output Cout_2
);

  Adder #(.width(2)) adder_1 (.a(A), .b(B), .out(out_7), .cin(Cin), .cout(Cout));
  // Probe on {Cout, out_7}
  Adder #(.width(3)) adder_2 (.a(in_4), .b(in_6), .out(out_8), .cin(Cin_2), .cout(Cout_2));
  // Probe on {Cout_2, out_8}

  // Notes on the sheet:
  //   2 bit full adder
  //   3 bit full adder
endmodule
