// Logisim project week5.circ as structural Verilog: 1 circuit, main circuit main
module main (
);

  wire clock_1_out, multiplexer_1_out, multiplexer_2_out, multiplexer_3_out, multiplexer_4_out,
       multiplexer_5_out, multiplexer_6_out, multiplexer_7_out, not_1_out;
  wire [3:0] counter_1_q;

  Clock clock_1 (.out(clock_1_out));
  // Probe on counter_1_q[3:1]
  // Probe on counter_1_q
  Counter #(.width(4), .max('hf)) counter_1 (.Q(counter_1_q), .clk(clock_1_out));  // open: load, D, count, carry, clr
  not not_1 (not_1_out, counter_1_q[0]);
  Multiplexer #(.select(3)) multiplexer_1 (
    .in0(not_1_out), .in1(1'b1), .in2(counter_1_q[0]), .in3(1'b1), .in4(1'b1), .in5(not_1_out),
    .in6(not_1_out), .in7(1'b1), .out(multiplexer_1_out), .sel(counter_1_q[3:1]));  // open: en
  Multiplexer #(.select(3)) multiplexer_2 (
    .in0(1'b1), .in1(1'b1), .in2(not_1_out), .in3(counter_1_q[0]), .in4(1'b1), .in5(not_1_out),
    .in6(counter_1_q[0]), .in7(1'b0), .out(multiplexer_2_out), .sel(counter_1_q[3:1]));  // open: en
  Multiplexer #(.select(3)) multiplexer_3 (
    .in0(1'b1), .in1(counter_1_q[0]), .in2(1'b1), .in3(1'b1), .in4(1'b1), .in5(1'b1), .in6(counter_1_q[0]),
    .in7(1'b0), .out(multiplexer_3_out), .sel(counter_1_q[3:1]));  // open: en
  _7_Segment_Display u_7_segment_display_1 (
    .g(multiplexer_7_out), .f(multiplexer_6_out), .a(multiplexer_1_out), .b(multiplexer_2_out),
    .e(multiplexer_5_out), .d(multiplexer_4_out), .c(multiplexer_3_out));  // open: dp
  Multiplexer #(.select(3)) multiplexer_4 (
    .in0(not_1_out), .in1(1'b1), .in2(counter_1_q[0]), .in3(not_1_out), .in4(1'b1), .in5(counter_1_q[0]),
    .in6(1'b1), .in7(not_1_out), .out(multiplexer_4_out), .sel(counter_1_q[3:1]));  // open: en
  Multiplexer #(.select(3)) multiplexer_5 (
    .in0(not_1_out), .in1(not_1_out), .in2(1'b0), .in3(not_1_out), .in4(not_1_out), .in5(1'b1), .in6(1'b1),
    .in7(1'b1), .out(multiplexer_5_out), .sel(counter_1_q[3:1]));  // open: en
  Multiplexer #(.select(3)) multiplexer_6 (
    .in0(not_1_out), .in1(1'b0), .in2(1'b1), .in3(not_1_out), .in4(1'b1), .in5(1'b1), .in6(not_1_out),
    .in7(1'b1), .out(multiplexer_6_out), .sel(counter_1_q[3:1]));  // open: en
  Multiplexer #(.select(3)) multiplexer_7 (
    .in0(1'b0), .in1(1'b1), .in2(1'b1), .in3(not_1_out), .in4(1'b1), .in5(1'b1), .in6(counter_1_q[0]),
    .in7(1'b1), .out(multiplexer_7_out), .sel(counter_1_q[3:1]));  // open: en

  // Notes on the sheet:
  //   A
  //   B
  //   C
  //   D
  //   E
  //   F
  //   G
endmodule
